// Logisim project RiskV.circ as structural Verilog: 13 circuits, main circuit ProgramCounter
module ProgramCounter (
  input  [31:0] TargetAddr,
  input  BranchCtl,
  input  Clk,
  input  Reset,
  output [31:0] PcOut,
  output [31:0] PcPlus4
);

  wire [31:0] multiplexer_1_out;

  Multiplexer #(.width(32)) multiplexer_1 (.in0(PcPlus4), .in1(TargetAddr), .out(multiplexer_1_out), .sel(BranchCtl));
  Register #(.width(32)) register_1 (.D(multiplexer_1_out), .en(1'b1), .clk(Clk), .Q(PcOut), .clr(Reset));
  Adder #(.width(32)) adder_1 (.a(32'h4), .b(PcOut), .out(PcPlus4));  // open: cin, cout
endmodule

module RegisterFile (
  input  [31:0] Data,
  input  [4:0] RdAddr,
  input  [4:0] Rs1Addr,
  input  [4:0] Rs2Addr,
  input  WriteEnable,
  input  Clk,
  output [31:0] Rs1Out,
  output [31:0] Rs2Out
);

  wire x1_we, x2_we, x3_we, x4_we, x5_we, x6_we, x7_we, x8_we, x9_we, x10_we, x11_we, x12_we, x13_we, x14_we,
       x15_we, x16_we, x17_we, x18_we, x19_we, x20_we, x21_we, x22_we, x23_we, x24_we, x25_we, x26_we,
       x27_we, x28_we, x29_we, x30_we, x31_we;
  wire [31:0] x1, x2, x3, x4, x5, x6, x7, x8, x9, x10, x11, x12, x13, x14, x15, x16, x17, x18, x19, x20, x21,
       x22, x23, x24, x25, x26, x27, x28, x29, x30, x31;

  Demultiplexer #(.select(5)) demultiplexer_1 (
    .out1(x1_we), .out2(x2_we), .out3(x3_we), .out4(x4_we), .out5(x5_we), .out6(x6_we), .out7(x7_we),
    .out8(x8_we), .out9(x9_we), .out10(x10_we), .out11(x11_we), .out12(x12_we), .out13(x13_we),
    .out14(x14_we), .out15(x15_we), .out16(x16_we), .out17(x17_we), .out18(x18_we), .out19(x19_we),
    .out20(x20_we), .out21(x21_we), .out22(x22_we), .out23(x23_we), .out24(x24_we), .out25(x25_we),
    .out26(x26_we), .out27(x27_we), .out28(x28_we), .out29(x29_we), .out30(x30_we), .out31(x31_we),
    .in(WriteEnable), .sel(RdAddr));  // open: out0
  Register #(.width(32)) register_1 (.D(Data), .en(x1_we), .clk(Clk), .Q(x1));  // open: clr
  Register #(.width(32)) register_2 (.D(Data), .en(x2_we), .clk(Clk), .Q(x2));  // open: clr
  Register #(.width(32)) register_3 (.D(Data), .en(x3_we), .clk(Clk), .Q(x3));  // open: clr
  Register #(.width(32)) register_4 (.D(Data), .en(x4_we), .clk(Clk), .Q(x4));  // open: clr
  Register #(.width(32)) register_5 (.D(Data), .en(x5_we), .clk(Clk), .Q(x5));  // open: clr
  Register #(.width(32)) register_6 (.D(Data), .en(x6_we), .clk(Clk), .Q(x6));  // open: clr
  Register #(.width(32)) register_7 (.D(Data), .en(x7_we), .clk(Clk), .Q(x7));  // open: clr
  Register #(.width(32)) register_8 (.D(Data), .en(x8_we), .clk(Clk), .Q(x8));  // open: clr
  Register #(.width(32)) register_9 (.D(Data), .en(x9_we), .clk(Clk), .Q(x9));  // open: clr
  Register #(.width(32)) register_10 (.D(Data), .en(x10_we), .clk(Clk), .Q(x10));  // open: clr
  Register #(.width(32)) register_11 (.D(Data), .en(x11_we), .clk(Clk), .Q(x11));  // open: clr
  Register #(.width(32)) register_12 (.D(Data), .en(x12_we), .clk(Clk), .Q(x12));  // open: clr
  Register #(.width(32)) register_13 (.D(Data), .en(x13_we), .clk(Clk), .Q(x13));  // open: clr
  Register #(.width(32)) register_14 (.D(Data), .en(x14_we), .clk(Clk), .Q(x14));  // open: clr
  Register #(.width(32)) register_15 (.D(Data), .en(x15_we), .clk(Clk), .Q(x15));  // open: clr
  Register #(.width(32)) register_16 (.D(Data), .en(x16_we), .clk(Clk), .Q(x16));  // open: clr
  Register #(.width(32)) register_17 (.D(Data), .en(x17_we), .clk(Clk), .Q(x17));  // open: clr
  Register #(.width(32)) register_18 (.D(Data), .en(x18_we), .clk(Clk), .Q(x18));  // open: clr
  Register #(.width(32)) register_19 (.D(Data), .en(x19_we), .clk(Clk), .Q(x19));  // open: clr
  Register #(.width(32)) register_20 (.D(Data), .en(x20_we), .clk(Clk), .Q(x20));  // open: clr
  Register #(.width(32)) register_21 (.D(Data), .en(x21_we), .clk(Clk), .Q(x21));  // open: clr
  Register #(.width(32)) register_22 (.D(Data), .en(x22_we), .clk(Clk), .Q(x22));  // open: clr
  Register #(.width(32)) register_23 (.D(Data), .en(x23_we), .clk(Clk), .Q(x23));  // open: clr
  Register #(.width(32)) register_24 (.D(Data), .en(x24_we), .clk(Clk), .Q(x24));  // open: clr
  Register #(.width(32)) register_25 (.D(Data), .en(x25_we), .clk(Clk), .Q(x25));  // open: clr
  Register #(.width(32)) register_26 (.D(Data), .en(x26_we), .clk(Clk), .Q(x26));  // open: clr
  Register #(.width(32)) register_27 (.D(Data), .en(x27_we), .clk(Clk), .Q(x27));  // open: clr
  Register #(.width(32)) register_28 (.D(Data), .en(x28_we), .clk(Clk), .Q(x28));  // open: clr
  Register #(.width(32)) register_29 (.D(Data), .en(x29_we), .clk(Clk), .Q(x29));  // open: clr
  Register #(.width(32)) register_30 (.D(Data), .en(x30_we), .clk(Clk), .Q(x30));  // open: clr
  Register #(.width(32)) register_31 (.D(Data), .en(x31_we), .clk(Clk), .Q(x31));  // open: clr
  Multiplexer #(.select(5), .width(32)) multiplexer_1 (
    .in0({32{1'b0}}), .in1(x1), .in2(x2), .in3(x3), .in4(x4), .in5(x5), .in6(x6), .in7(x7), .in8(x8),
    .in9(x9), .in10(x10), .in11(x11), .in12(x12), .in13(x13), .in14(x14), .in15(x15), .in16(x16), .in17(x17),
    .in18(x18), .in19(x19), .in20(x20), .in21(x21), .in22(x22), .in23(x23), .in24(x24), .in25(x25),
    .in26(x26), .in27(x27), .in28(x28), .in29(x29), .in30(x30), .in31(x31), .out(Rs1Out), .sel(Rs1Addr));
  Multiplexer #(.select(5), .width(32)) multiplexer_2 (
    .in0({32{1'b0}}), .in1(x1), .in2(x2), .in3(x3), .in4(x4), .in5(x5), .in6(x6), .in7(x7), .in8(x8),
    .in9(x9), .in10(x10), .in11(x11), .in12(x12), .in13(x13), .in14(x14), .in15(x15), .in16(x16), .in17(x17),
    .in18(x18), .in19(x19), .in20(x20), .in21(x21), .in22(x22), .in23(x23), .in24(x24), .in25(x25),
    .in26(x26), .in27(x27), .in28(x28), .in29(x29), .in30(x30), .in31(x31), .out(Rs2Out), .sel(Rs2Addr));

  // Other names for the same wires on the sheet: rd[4:0] = RdAddr; rs1[4:0] = Rs1Addr; rs2[4:0] = Rs2Addr;
  //   we_in = WriteEnable
endmodule

module MainController (
  input  [31:0] Inst,
  output [2:0] ImmSel,
  output ASel,
  output BSel,
  output [3:0] ALUSel,
  output [4:0] BrSel,
  output MemRead,
  output MemWrite,
  output [2:0] MemByteSel,
  output RegWEn,
  output [1:0] WBSel,
  output Is_Ecall,
  output Is_Ebreak
);

  wire ALUSel0Mod, and_1_out, and_2_out, AUIPC, I_Type, Is_Arith, is_sys, JALR, Load, LUI, nand_1_out,
       not_1_out, or_4_out, or_5_out, or_8_out, R_Type, Store, System;
  wire [0:0] and_15_out;
  wire [2:0] bit_extender_1_out;
  wire [3:0] bit_extender_2_out;

  nand nand_1 (nand_1_out, Inst[12], Inst[13], Inst[14]);
  and and_1 (and_1_out, Inst[12], ~Inst[13], Inst[14]);  // AND_Gate
  or or_1 (Is_Arith, I_Type, R_Type);
  and and_2 (and_2_out, System, nand_1_out);
  or or_2 (ALUSel0Mod, and_1_out, R_Type);
  // Probe on Inst[6:0]
  // Probe on Inst[14:12]
  // Probe on Inst[31:25]
  and and_3 (Is_Ebreak, Inst[20], and_2_out);
  and and_4 (Is_Ecall, and_2_out, not_1_out);
  not not_1 (not_1_out, Inst[20]);
  and and_5 (R_Type, Inst[0], Inst[1], ~Inst[2], ~Inst[3], Inst[4], Inst[5], ~Inst[6]);  // AND_Gate
  and and_6 (I_Type, Inst[0], Inst[1], ~Inst[2], ~Inst[3], Inst[4], ~Inst[5], ~Inst[6]);  // AND_Gate
  and and_7 (Load, Inst[0], Inst[1], ~Inst[2], ~Inst[3], ~Inst[4], ~Inst[5], ~Inst[6]);  // AND_Gate
  and and_8 (Store, Inst[0], Inst[1], ~Inst[2], ~Inst[3], ~Inst[4], Inst[5], ~Inst[6]);  // AND_Gate
  and and_9 (ImmSel[2], Inst[0], Inst[1], Inst[2], Inst[3], ~Inst[4], Inst[5], Inst[6]);  // AND_Gate
  and and_10 (BrSel[1], Inst[0], Inst[1], ~Inst[2], ~Inst[3], ~Inst[4], Inst[5], Inst[6]);  // AND_Gate
  and and_11 (AUIPC, Inst[0], Inst[1], Inst[2], ~Inst[3], Inst[4], ~Inst[5], ~Inst[6]);  // AND_Gate
  and and_12 (LUI, Inst[0], Inst[1], Inst[2], ~Inst[3], Inst[4], Inst[5], ~Inst[6]);  // AND_Gate
  and and_13 (System, Inst[0], Inst[1], ~Inst[2], ~Inst[3], Inst[4], Inst[5], Inst[6]);  // AND_Gate
  and and_14 (JALR, Inst[0], Inst[1], Inst[2], ~Inst[3], ~Inst[4], Inst[5], Inst[6]);  // AND_Gate
  or or_3 (is_sys, Is_Ecall, Is_Ebreak);
  assign bit_extender_1_out = {{2{or_4_out}}, or_4_out};  // Bit_Extender bit_extender_1
  or or_4 (or_4_out, Load, Store);
  or or_5 (or_5_out, LUI, AUIPC);
  or or_6 (ImmSel[1], or_5_out, BrSel[1]);
  and and_15 (and_15_out[0], ALUSel0Mod, Inst[30]);
  or or_7 (BrSel[0], ImmSel[2], JALR);
  and and_16 (MemRead, Load, ~is_sys);  // AND_Gate
  and and_17 (MemWrite, Store, ~is_sys);  // AND_Gate
  assign MemByteSel = bit_extender_1_out & {Inst[13:12], Inst[14]};  // AND_Gate and_18, 3 bits wide
  or or_8 (or_8_out, R_Type, I_Type, Load, LUI, AUIPC, ImmSel[2], JALR);
  not not_2 (WBSel[0], Load);
  or or_9 (WBSel[1], ImmSel[2], JALR);
  or or_10 (ImmSel[0], or_5_out, Store);
  assign bit_extender_2_out = {{3{Is_Arith}}, Is_Arith};  // Bit_Extender bit_extender_2
  assign ALUSel = bit_extender_2_out & {Inst[14:12], and_15_out[0]};  // AND_Gate and_19, 4 bits wide
  and and_20 (RegWEn, or_8_out, ~is_sys);  // AND_Gate
  or or_11 (ASel, AUIPC, ImmSel[2], BrSel[1]);
  or or_12 (BSel, LUI, Store, Load, I_Type, AUIPC, ImmSel[2], JALR, BrSel[1]);

  assign BrSel[4:2] = Inst[14:12];

  // Other names for the same wires on the sheet: Branch = BrSel[1]; func3[2:0] = Inst[14:12]; ebreak = Is_Ebreak;
  //   ecall = Is_Ecall; JAL = ImmSel[2]; op_code[6:0] = Inst[6:0]; func7[6:0] = Inst[31:25]

  // Notes on the sheet:
  //   ALUSel0Mode = R_Type OR IShift_Right
  //   Is_Arithmetic = R_Type OR I_Type
  //   Funct3 == 000
  //   SYSTEM_CTL
  //   R_TYPE == 011 0011
  //   I_Type == 001 0011
  //   Load == 000 0011
  //   Store == 010 0011
  //   JAL == 110 1111
  //   Branch == 110 0011
  //   AUIPC == 001 0111
  //   LUI == 011 0111
  //   SYSTEM == 1110011
  //   JALR == 110 0111
  //   ID_Control
  //   EX_Control
  //   MEM_Control
  //   WB_Control
  //   Trap_Control
  //   MemByteSel[0] = func3[2]
  //   MemByteSel[1] = func3[0]
  //   MemByteSel[2] = func3[1]
  //   (1 bit): Breakpoint trap flag.
  //   (3bit):  Send to ImmGen Sel input
  //   ImmSel[0] = Store OR LUI OR AUIPC
  //   ImmSel[1] = Branch OR LUI OR AUIPC
  //   ImmSel[2] = JAL
  //   (1 bit): Selects ALU operand A
  //   ASel = AUIPC OR Branch OR JAL
  //   ALUSel[1] = funct3[0]
  //   ALUSel[2] = funct3[1]
  //   ALUSel[3] = funct3[2]
  //   (1 bit): Enables Data Memory read operations.
  //   (1 bit): Enables Data Memory write operations.
  //   (1 bit): Master write-enable for the register file.
  //   (2 bit): Selects the writeback source (ALU result vs. Memory read data).
  //   (1 bit): Selects the writeback source (ALU result vs. Memory read data).
  //   (1 bit): Selects ALU operand B (Register vs. Immediate).
  //   BSel = IType OR Load OR Store OR AUIPC OR JAL OR JALR
  //   ALUSel[0] = funct7[5] AND (RType OR IShift_Right)
  //   (4bit): 3 Bit branch selector code sent directly to the BranchControl
  //   (3bit): Bus to control which bytes are active during memory read and write
  //   (4 bits): Sent directly to ALUSel bus Top 3 bits from funct3 LSB from funct7[5]
endmodule

module BranchController (
  input  [31:0] dataA,
  input  [31:0] dataB,
  input  [4:0] BrSel,
  output TakeBranch
);

  wire adder_1_cout, and_1_out, branchselector_1_takebranch, wordlevelcomparator_1_eq,
       wordlevelcomparator_1_lts, wordlevelcomparator_1_ltu;
  wire [31:0] adder_1_out, not_1_out;

  assign not_1_out = ~dataB;  // NOT_Gate not_1, 32 bits wide
  Adder #(.width(32)) adder_1 (.a(dataA), .b(not_1_out), .out(adder_1_out), .cin(1'b1), .cout(adder_1_cout));
  WordLevelComparator wordlevelcomparator_1 (
    .InSum(adder_1_out), .InCout(adder_1_cout), .ASignIn(dataA[31]), .BSignIn(dataB[31]),
    .EQ(wordlevelcomparator_1_eq), .LTU(wordlevelcomparator_1_ltu), .LTS(wordlevelcomparator_1_lts));
  BranchSelector branchselector_1 (
    .EQ(wordlevelcomparator_1_eq), .LTS(wordlevelcomparator_1_lts), .LTU(wordlevelcomparator_1_ltu),
    .sel(BrSel[4:2]), .TakeBranch(branchselector_1_takebranch));
  and and_1 (and_1_out, branchselector_1_takebranch, BrSel[1]);
  or or_1 (TakeBranch, and_1_out, BrSel[0]);

  // Other names for the same wires on the sheet: ASign = dataA[31]; BSign = dataB[31]
endmodule

module WordLevelComparator (
  input  [31:0] InSum,
  input  InCout,
  input  ASignIn,
  input  BSignIn,
  output EQ,
  output LTU,
  output LTS
);

  wire or_1_out, xor_1_out;

  not not_1 (LTU, InCout);
  xor xor_1 (xor_1_out, ASignIn, BSignIn);
  Multiplexer multiplexer_1 (.in0(LTU), .in1(ASignIn), .out(LTS), .sel(xor_1_out));
  or or_1 (or_1_out, InSum[0], InSum[1], InSum[2], InSum[3], InSum[4], InSum[5], InSum[6], InSum[7], InSum[8], InSum[9], InSum[10], InSum[11], InSum[12], InSum[13], InSum[14], InSum[15], InSum[16], InSum[17], InSum[18], InSum[19], InSum[20], InSum[21], InSum[22], InSum[23], InSum[24], InSum[25], InSum[26], InSum[27], InSum[28], InSum[29], InSum[30], InSum[31]);
  not not_2 (EQ, or_1_out);
endmodule

module BranchSelector (
  input  EQ,
  input  LTS,
  input  LTU,
  input  [2:0] sel,
  output TakeBranch
);

  wire not_1_out, or_1_out, or_2_out;

  not not_1 (not_1_out, EQ);
  or or_1 (or_1_out, ~LTS, EQ);  // OR_Gate
  or or_2 (or_2_out, ~LTU, EQ);  // OR_Gate
  Multiplexer #(.select(3)) multiplexer_1 (
    .in0(EQ), .in1(not_1_out), .in2(1'b0), .in3(1'b0), .in4(LTS), .in5(or_1_out), .in6(LTU), .in7(or_2_out),
    .out(TakeBranch), .sel(sel));
endmodule

module ImmGen (
  input  [31:0] InstIn,
  input  [2:0] ImmSelIn,
  output [31:0] ImmOut
);

  Multiplexer #(.select(3), .width(32)) multiplexer_1 (
    .in0({{21{InstIn[31]}}, InstIn[30:20]}), .in1({{21{InstIn[31]}}, InstIn[30:25], InstIn[11:7]}),
    .in2({{20{InstIn[31]}}, InstIn[7], InstIn[30:25], InstIn[11:8], 1'b0}),
    .in3({InstIn[31:12], {12{1'b0}}}),
    .in4({{12{InstIn[31]}}, InstIn[19:12], InstIn[20], InstIn[30:21], 1'b0}), .out(ImmOut), .sel(ImmSelIn));  // open: in5, in6, in7

  // Other names for the same wires on the sheet: BType[31:1] = {{20{InstIn[31]}}, InstIn[7], InstIn[30:25], InstIn[11:8]};
  //   Ins8 = InstIn[8]; SType[31:0] = {{21{InstIn[31]}}, InstIn[30:25], InstIn[11:7]}; Ins9 = InstIn[9];
  //   Ins10 = InstIn[10]; Ins11 = InstIn[11]; Ins7 = InstIn[7]; ImmSel[2:0] = ImmSelIn; Ins0 = InstIn[0];
  //   Ins1 = InstIn[1]; Ins2 = InstIn[2]; Ins3 = InstIn[3]; Ins4 = InstIn[4]; Ins5 = InstIn[5]; Ins6 = InstIn[6];
  //   Ins21 = InstIn[21]; IType[31:0] = {{21{InstIn[31]}}, InstIn[30:20]};
  //   JType[31:1] = {{12{InstIn[31]}}, InstIn[19:12], InstIn[20], InstIn[30:21]}; UType[31:12] = InstIn[31:12];
  //   Ins22 = InstIn[22]; Ins23 = InstIn[23]; Ins24 = InstIn[24]; Ins25 = InstIn[25]; Ins26 = InstIn[26];
  //   Ins27 = InstIn[27]; Ins28 = InstIn[28]; Ins29 = InstIn[29]; Ins30 = InstIn[30]; Ins20 = InstIn[20];
  //   Ins12 = InstIn[12]; Ins13 = InstIn[13]; Ins14 = InstIn[14]; Ins15 = InstIn[15]; Ins16 = InstIn[16];
  //   Ins17 = InstIn[17]; Ins18 = InstIn[18]; Ins19 = InstIn[19]; Ins31 = InstIn[31]

  // Notes on the sheet:
  //   I-Type
  //   S-Type
  //   B-Type
  //   U-Type
  //   J-Type
endmodule

module RiskVCPUSingleCycle (
  input  in_1
);

  wire ASel, BSel, ebreak, ecall, MemRead, MemWrite, PCSel, RegWEn, SysClk;
  wire [1:0] AddrOffset, WBSel;
  wire [2:0] ImmSel, MemByteSel;
  wire [3:0] ALUSel, StoreMask;
  wire [4:0] BrSel;
  wire [31:0] ALUDataSrcA, ALUDataSrcB, ImmGenOut, Inst, MemInAligned, MemOut, MemOutAligned, PC, PCPlus4,
       RDataA, RDataB, RegWBData;
  wire [31:2] ALUOut;

  Clock clock_1 (.out(SysClk));
  // Probe on PC[11:2]
  ROM #(.addrWidth(10), .dataWidth(32)) IMem (.addr(PC[11:2]), .data(Inst));
  // Probe on PC
  // Probe on PCPlus4
  // Probe on Inst
  ProgramCounter programcounter_1 (
    .TargetAddr({ALUOut, AddrOffset}), .BranchCtl(PCSel), .Clk(SysClk), .Reset(in_1), .PcOut(PC),
    .PcPlus4(PCPlus4));
  // Probe on Inst[11:7]
  // Probe on Inst[19:15]
  // Probe on Inst[24:20]
  // Probe on ImmGenOut
  // Probe on RDataA
  // Probe on RDataB
  // Probe on RegWBData
  MainController maincontroller_1 (
    .Inst(Inst), .ImmSel(ImmSel), .ASel(ASel), .BSel(BSel), .ALUSel(ALUSel), .BrSel(BrSel),
    .MemRead(MemRead), .MemWrite(MemWrite), .MemByteSel(MemByteSel), .RegWEn(RegWEn), .WBSel(WBSel),
    .Is_Ecall(ecall), .Is_Ebreak(ebreak));
  ImmGen immgen_1 (.InstIn(Inst), .ImmSelIn(ImmSel), .ImmOut(ImmGenOut));
  RegisterFile registerfile_1 (
    .Data(RegWBData), .RdAddr(Inst[11:7]), .Rs1Addr(Inst[19:15]), .Rs2Addr(Inst[24:20]),
    .WriteEnable(RegWEn), .Clk(SysClk), .Rs1Out(RDataA), .Rs2Out(RDataB));
  // Probe on ImmSel
  // Probe on ASel
  // Probe on BSel
  // Probe on ALUSel
  // Probe on BrSel
  // Probe on MemRead
  // Probe on MemWrite
  // Probe on MemByteSel
  // Probe on RegWEn
  // Probe on WBSel
  // Probe on ecall
  // Probe on ebreak
  // Probe on PCSel
  // Probe on {ALUOut, AddrOffset}
  // Probe on ALUDataSrcA
  // Probe on ALUDataSrcB
  BranchController branchcontroller_1 (.dataA(RDataA), .dataB(RDataB), .BrSel(BrSel), .TakeBranch(PCSel));
  ALU alu_1 (.dataA(ALUDataSrcA), .dataB(ALUDataSrcB), .sel(ALUSel), .Out0({ALUOut, AddrOffset}));
  ALUDataSource aludatasource_1 (
    .RDataA(RDataA), .PC(PC), .ASel(ASel), .RDataB(RDataB), .ImmVal(ImmGenOut), .BSel(BSel),
    .DataA(ALUDataSrcA), .DataB(ALUDataSrcB));
  // Probe on ALUOut[11:2]
  RAM #(.addrWidth(10), .asyncread("true"), .byteenables("byteEnables"), .dataWidth(32)) DMem (
    .addr(ALUOut[11:2]), .we(MemWrite), .oe(MemRead), .clk(SysClk), .din(MemInAligned), .dout(MemOut),
    .be3(StoreMask[3]), .be2(StoreMask[2]), .be1(StoreMask[1]), .be0(StoreMask[0]));
  // Probe on MemInAligned
  // Probe on RDataB
  // Probe on AddrOffset
  // Probe on MemByteSel
  // Probe on MemOut
  // Probe on MemInAligned
  // Probe on MemOutAligned
  StoreAligner storealigner_1 (
    .Data(RDataB), .AddrOffset(AddrOffset), .ByteSel(MemByteSel), .DataOut(MemInAligned), .MaskOut(StoreMask));
  LoadAligner loadaligner_1 (.AddrOffset(AddrOffset), .Data(MemOut), .ByteSel(MemByteSel), .Out0(MemOutAligned));
  Multiplexer #(.select(2), .width(32)) multiplexer_1 (
    .in0(MemOutAligned), .in1({ALUOut, AddrOffset}), .in3(PCPlus4), .out(RegWBData), .sel(WBSel));  // open: in2
  // Probe on RegWBData

  // Other names for the same wires on the sheet: ALUOut[1:0] = AddrOffset; rdi[4:0] = Inst[11:7];
  //   rs1[4:0] = Inst[19:15]; rs2[4:0] = Inst[24:20]; Reset = in_1

  // Notes on the sheet:
  //   contents of IMem (hex, n*v repeats v):
  //   1117 10113 297 25828293 317 7f030313 397 7f038393 735c63 2ae03 1c32023 428293 430313 fedff06f 297
  //   7d028293 317 7c830313 62d863 2a023 428293 ff5ff06f 44000ef 6f 40006f 6f ff010113 b12423 a12623
  //   40006f 812503 c12583 a5a023 1010113 8067 50593 5a503 45a583 8067 ff010113 112623 1537 80850513
  //   a12023 637 1e060613 6400593 97 fac080e7 12503 450513 637 20060613 c800593 b12223 97 f8c080e7 500513
  //   a00593 97 80080e7 50593 637 21060613 513 97 f64080e7 412583 537 26050613 c12423 26052503 97 54080e7
  //   50593 637 22060613 400513 97 f30080e7 812503 97 38080e7 50593 637 23060613 800513 97 f0c080e7 40006f
  //   6f b50533 8067 40b50533 8067 ff010113 112623 a12023 5b7 24058593 97 efc080e7 12503 b12223 5b7
  //   25058593 97 ee4080e7 50613 412503 c12423 812583 97 fac080e7 c12083 1010113 8067 2f637273 1d40073
  //   IF - Instruction Fetch
  //   ID - Instruction Decode
  //   EX - Execute
  //   MEM - Memory
  //   WB - Write Back
  //   00 = Mem
  //   01 = ALU
  //   11 = PCPlus4
endmodule

module ALU (
  input  [31:0] dataA,
  input  [31:0] dataB,
  input  [3:0] sel,
  output [31:0] Out0
);

  wire comparator_1_lt, comparator_2_lt;
  wire [31:0] add_t, and_t, or_t, sll_t, slt_t, sltu_t, sra_t, srl_t, sub_t, xor_t;

  Adder #(.width(32)) adder_1 (.a(dataA), .b(dataB), .out(add_t));  // open: cin, cout
  Subtractor #(.width(32)) subtractor_1 (.a(dataA), .b(dataB), .out(sub_t));  // open: bin, bout
  Shifter #(.width(32)) shifter_1 (.in(dataA), .\dist (dataB[4:0]), .out(sll_t));
  Shifter #(.shift("lr"), .width(32)) shifter_2 (.in(dataA), .\dist (dataB[4:0]), .out(srl_t));
  Shifter #(.shift("ar"), .width(32)) shifter_3 (.in(dataA), .\dist (dataB[4:0]), .out(sra_t));
  assign and_t = dataA & dataB;  // AND_Gate and_1, 32 bits wide
  assign or_t = dataA | dataB;  // OR_Gate or_1, 32 bits wide
  assign xor_t = dataA ^ dataB;  // XOR_Gate xor_1, 32 bits wide
  Comparator #(.width(32)) comparator_1 (.a(dataA), .b(dataB), .lt(comparator_1_lt));  // open: gt, eq
  Comparator #(.width(32)) comparator_2 (.a(dataA), .b(dataB), .lt(comparator_2_lt));  // open: gt, eq
  assign slt_t = {{31{1'b0}}, comparator_1_lt};  // Bit_Extender bit_extender_1
  assign sltu_t = {{31{1'b0}}, comparator_2_lt};  // Bit_Extender bit_extender_2
  Multiplexer #(.select(4), .width(32)) multiplexer_1 (
    .in0(add_t), .in1(sub_t), .in2(sll_t), .in4(slt_t), .in6(sltu_t), .in8(xor_t), .in10(srl_t),
    .in11(sra_t), .in12(or_t), .in14(and_t), .out(Out0), .sel(sel));  // open: in3, in5, in7, in9, in13, in15
  // Probe on sel

  // Other names for the same wires on the sheet: shamt[4:0] = dataB[4:0]

  // Notes on the sheet:
  //   Select control
  //   add = 0000
  //   sub = 0001
  //   sll = 0010
  //   slt = 0100
  //   sltu = 0110
  //   xor = 1000
  //   srl = 1010
  //   sra = 1011
  //   or = 1100
  //   and = 1110
endmodule

module ALUDataSource (
  input  [31:0] RDataA,
  input  [31:0] PC,
  input  ASel,
  input  [31:0] RDataB,
  input  [31:0] ImmVal,
  input  BSel,
  output [31:0] DataA,
  output [31:0] DataB
);

  Multiplexer #(.width(32)) multiplexer_1 (.in0(RDataA), .in1(PC), .out(DataA), .sel(ASel));
  Multiplexer #(.width(32)) multiplexer_2 (.in0(RDataB), .in1(ImmVal), .out(DataB), .sel(BSel));
endmodule

module LoadAligner (
  input  [1:0] AddrOffset,
  input  [31:0] Data,
  input  [2:0] ByteSel,
  output [31:0] Out0
);

  wire and_3_out, B, missAlign;
  wire [4:3] shamt;
  wire [31:0] lb, lbu, lh, lhu, shiftedData;

  // Probe on Data
  // Probe on AddrOffset
  // Probe on ByteSel
  and and_1 (B, ~ByteSel[1], ~ByteSel[2]);  // AND_Gate
  and and_2 (missAlign, AddrOffset[0], ~AddrOffset[1], ByteSel[1], ~ByteSel[2]);  // AND_Gate
  and and_3 (and_3_out, ~AddrOffset[0], B, ~ByteSel[2]);  // AND_Gate
  or or_1 (shamt[3], and_3_out, missAlign);
  and and_4 (shamt[4], ~AddrOffset[1], ~ByteSel[2], ~missAlign);  // AND_Gate
  Shifter #(.shift("lr"), .width(32)) shifter_1 (.in(Data), .\dist ({shamt, 3'b000}), .out(shiftedData));
  // Probe on {shamt, 3'b000}
  // Probe on shiftedData
  assign lb = {{24{shiftedData[7]}}, shiftedData[7:0]};  // Bit_Extender bit_extender_1
  assign lbu = {{24{1'b0}}, shiftedData[7:0]};  // Bit_Extender bit_extender_2
  assign lh = {{16{shiftedData[15]}}, shiftedData[15:0]};  // Bit_Extender bit_extender_3
  assign lhu = {{16{1'b0}}, shiftedData[15:0]};  // Bit_Extender bit_extender_4
  Multiplexer #(.select(3), .width(32)) multiplexer_1 (
    .in0(lb), .in1(lbu), .in2(lh), .in3(lhu), .in4(Data), .out(Out0), .sel(ByteSel));  // open: in5, in6, in7
  // Probe on ByteSel

  // Other names for the same wires on the sheet: offset0 = AddrOffset[0]; offset1 = AddrOffset[1]; H = ByteSel[1];
  //   W = ByteSel[2]; dataIn[31:0] = Data

  // Notes on the sheet:
  //   Signed Byte = 000
  //   Unsigned Byte = 001
  //   Signed Half Word = 010
  //   Unsigned Half Word = 011
  //   Full Word = 100
  //   Shift data by address offset amount
endmodule

module StoreMaskGenerator (
  input  [1:0] AddrOffset,
  input  [2:0] ByteSel,
  output [3:0] OutMask
);

  wire A0_AND_B, A0_OR_H, A1_AND_NOT_A0_AND_B, A1_XOR_A0, and_5_out, and_6_out, and_7_out, and_8_out,
       and_9_out, B, B_OR_H, NOT_A0, NOT_A0_AND_H, NOT_A1, or_3_out, or_4_out, or_5_out;

  not not_1 (NOT_A0, AddrOffset[0]);
  not not_2 (NOT_A1, AddrOffset[1]);
  and and_1 (B, ~ByteSel[1], ~ByteSel[2]);  // AND_Gate
  and and_2 (NOT_A0_AND_H, NOT_A0, ByteSel[1]);
  and and_3 (A0_AND_B, AddrOffset[0], B);
  or or_1 (B_OR_H, B, ByteSel[1]);
  and and_4 (A1_AND_NOT_A0_AND_B, AddrOffset[1], NOT_A0, B);
  xor xor_1 (A1_XOR_A0, AddrOffset[1], AddrOffset[0]);
  or or_2 (A0_OR_H, ByteSel[1], AddrOffset[0]);
  and and_5 (and_5_out, AddrOffset[1], or_3_out);
  or or_3 (or_3_out, A0_AND_B, ByteSel[1]);
  and and_6 (and_6_out, A1_XOR_A0, ByteSel[1]);
  and and_7 (and_7_out, NOT_A1, or_4_out);
  or or_4 (or_4_out, NOT_A0_AND_H, A0_AND_B);
  and and_8 (and_8_out, NOT_A1, and_9_out);
  and and_9 (and_9_out, NOT_A0, B_OR_H);
  or or_5 (or_5_out, A1_AND_NOT_A0_AND_B, and_6_out);
  or or_6 (OutMask[1], or_5_out, ByteSel[2]);
  or or_7 (OutMask[3], and_8_out, ByteSel[2]);
  or or_8 (OutMask[0], and_5_out, ByteSel[2]);
  or or_9 (OutMask[2], and_7_out, A0_OR_H, ByteSel[2]);

  // Other names for the same wires on the sheet: A0 = AddrOffset[0]; A1 = AddrOffset[1]; H = ByteSel[1];
  //   W = ByteSel[2]

  // Notes on the sheet:
  //   Mask[0] = W OR (A1 AND (A0 AND B OR H))
  //   Mask[1] = W OR (A1 AND ~A0 AND B) OR (H AND (A1 XOR A0))
  //   Mask[2] = W OR (~A1 AND (A0 AND B OR ~A0 AND H))
  //   Mask[3] = W OR (~A1 AND (~A0 AND B OR H))
endmodule

module StoreAligner (
  input  [31:0] Data,
  input  [1:0] AddrOffset,
  input  [2:0] ByteSel,
  output [31:0] DataOut,
  output [3:0] MaskOut
);

  wire and_3_out, B, missAlign;
  wire [4:3] shamt;

  // Probe on Data
  // Probe on AddrOffset
  // Probe on ByteSel
  and and_1 (B, ~ByteSel[1], ~ByteSel[2]);  // AND_Gate
  and and_2 (missAlign, AddrOffset[0], ~AddrOffset[1], ByteSel[1], ~ByteSel[2]);  // AND_Gate
  and and_3 (and_3_out, ~AddrOffset[0], B, ~ByteSel[2]);  // AND_Gate
  or or_1 (shamt[3], and_3_out, missAlign);
  and and_4 (shamt[4], ~AddrOffset[1], ~ByteSel[2], ~missAlign);  // AND_Gate
  // Probe on MaskOut
  StoreMaskGenerator storemaskgenerator_1 (.AddrOffset(AddrOffset), .ByteSel(ByteSel), .OutMask(MaskOut));
  // Probe on {shamt, 3'b000}
  // Probe on DataOut
  Shifter #(.width(32)) shifter_1 (.in(Data), .\dist ({shamt, 3'b000}), .out(DataOut));

  // Other names for the same wires on the sheet: offset0 = AddrOffset[0]; offset1 = AddrOffset[1];
  //   dataIn[31:0] = Data; MemByteSel[2:0] = ByteSel; H = ByteSel[1]; W = ByteSel[2]; shiftedData[31:0] = DataOut;
  //   StoreMask[3:0] = MaskOut

  // Notes on the sheet:
  //   Shift data by address offset amount
endmodule
