// Logisim project RiskVALU.circ as structural Verilog: 4 circuits, main circuit ALUBase
module ALUBase (
  input  [31:0] dataA,
  input  [31:0] dataB,
  input  [3:0] sel,
  output [31:0] Out0
);

  wire comparator_1_lt, comparator_2_lt;
  wire [31:0] add_t, and_t, or_t, sll_t, slt_t, sltu_t, sra_t, srl_t, sub_t, xor_t;

  Adder #(.width(32)) adder_1 (.a(dataA), .b(dataB), .out(add_t));  // open: cin, cout
  Subtractor #(.width(32)) subtractor_1 (.a(dataA), .b(dataB), .out(sub_t));  // open: bin, bout
  Shifter #(.width(32)) shifter_1 (.in(dataA), .\dist (dataB[4:0]), .out(sll_t));
  Shifter #(.shift("lr"), .width(32)) shifter_2 (.in(dataA), .\dist (dataB[4:0]), .out(srl_t));
  Shifter #(.shift("ar"), .width(32)) shifter_3 (.in(dataA), .\dist (dataB[4:0]), .out(sra_t));
  assign and_t = dataA & dataB;  // AND_Gate and_1, 32 bits wide
  assign or_t = dataA | dataB;  // OR_Gate or_1, 32 bits wide
  assign xor_t = dataA ^ dataB;  // XOR_Gate xor_1, 32 bits wide
  Comparator #(.width(32)) comparator_1 (.a(dataA), .b(dataB), .lt(comparator_1_lt));  // open: gt, eq
  Comparator #(.width(32)) comparator_2 (.a(dataA), .b(dataB), .lt(comparator_2_lt));  // open: gt, eq
  assign slt_t = {{31{1'b0}}, comparator_1_lt};  // Bit_Extender bit_extender_1
  assign sltu_t = {{31{1'b0}}, comparator_2_lt};  // Bit_Extender bit_extender_2
  Multiplexer #(.select(4), .width(32)) multiplexer_1 (
    .in0(add_t), .in1(sll_t), .in2(slt_t), .in3(sltu_t), .in4(xor_t), .in5(srl_t), .in6(or_t), .in7(and_t),
    .in8(sub_t), .in13(sra_t), .out(Out0), .sel(sel));  // open: in9, in10, in11, in12, in14, in15
  // Probe on sel

  // Other names for the same wires on the sheet: shamt[4:0] = dataB[4:0]

  // Notes on the sheet:
  //   sel[3] = func7[5]
  //   sel[2:0] = func3
  //   Select control
  //   Select control
  //   add = 0000
  //   sll = 0001
  //   slt = 0010
  //   sltu = 0011
  //   xor = 0100
  //   srl = 0101
  //   or = 0110
  //   and = 0111
  //   sub = 1000
  //   sra = 1101
endmodule

module ALUDataSource (
  input  [31:0] RDataA,
  input  [31:0] PC,
  input  ASel,
  input  [31:0] RDataB,
  input  [31:0] ImmVal,
  input  BSel,
  output [31:0] DataA,
  output [31:0] DataB
);

  Multiplexer #(.width(32)) multiplexer_1 (.in0(RDataA), .in1(PC), .out(DataA), .sel(ASel));
  Multiplexer #(.width(32)) multiplexer_2 (.in0(RDataB), .in1(ImmVal), .out(DataB), .sel(BSel));
endmodule

module ALUControl (
  input  [31:0] RDataA,
  input  [31:0] PC,
  input  ASel,
  input  [31:0] RDataB,
  input  [31:0] ImmVal,
  input  BSel,
  input  [4:0] ALUSel,
  output [31:0] Out0
);

  wire [31:0] baseOut, dataA, dataB, mulDivOut;

  ALUDataSource aludatasource_1 (
    .RDataA(RDataA), .PC(PC), .ASel(ASel), .RDataB(RDataB), .ImmVal(ImmVal), .BSel(BSel), .DataA(dataA),
    .DataB(dataB));
  ALUMulDiv alumuldiv_1 (.dataA(dataA), .dataB(dataB), .sel(ALUSel[2:0]), .Out0(mulDivOut));
  ALUBase alubase_1 (.dataA(dataA), .dataB(dataB), .sel(ALUSel[3:0]), .Out0(baseOut));
  Multiplexer #(.select(2), .width(32)) multiplexer_1 (
    .in0(baseOut), .in1(baseOut), .out(Out0), .sel(ALUSel[4:3]));  // open: in2, in3

  // Other names for the same wires on the sheet: sel[4:0] = ALUSel

  // Notes on the sheet:
  //   sel[4:3] = func7[0] func7[5]
  //   sel[2:0] = func3
  //   Select control
endmodule

module ALUMulDiv (
  input  [31:0] dataA,
  input  [31:0] dataB,
  input  [2:0] sel,
  output [31:0] Out0
);

  wire [31:0] div, divu, mul, mulh, mulhsu, mulhu, multiplexer_1_out, rem_t, remu;

  Multiplexer #(.select(3), .width(32)) multiplexer_1 (
    .in0(mul), .in1(mulh), .in2(mulhsu), .in3(mulhu), .in4(div), .in5(divu), .in6(rem_t), .in7(remu),
    .out(multiplexer_1_out), .sel(sel));
  // Probe on sel

  // Notes on the sheet:
  //   Select control
  //   sel[2:0] = func3
  //   mul = 000
  //   mulh = 001
  //   mulhsu = 010
  //   mulhu = 011
  //   div = 100
  //   divu = 101
  //   rem = 110
  //   remu = 111
  //   Select control
endmodule
