// Logisim project RiskVCPU.circ as structural Verilog: 1 circuit, main circuit RiskVCPU
module RiskVCPU (
  input  SysClk,
  input  EXT_CTL_EN,
  input  [31:0] Inst,
  input  [31:0] MemOutData,
  input  HALT,
  output [31:0] IMemPC,
  output [31:0] DMemAddr,
  output DMemWE,
  output DMemRead,
  output [3:0] DMemMask,
  output [31:0] DMemWriteData,
  output [31:0] TEST_Out,
  output [31:0] TEST_instret
);

  wire ASel, BSel, clock_1_out, ebreak, ecall, EX_MEM_ebreak, EX_MEM_ecall, EX_MEM_RegWEn, EX_MEM_valid,
       ID_EX_ASel, ID_EX_BSel, ID_EX_ebreak, ID_EX_ecall, ID_EX_FLUSH, ID_EX_MemRead, ID_EX_MemWrite,
       ID_EX_RegWEn, ID_EX_valid, IF_ID_FLUSH, IF_ID_valid, IF_ID_WE, MEM_WB_ebreak, MEM_WB_ecall,
       MEM_WB_RegWEn, MEM_WB_valid, MemRead, MemWrite, PC_WE, PCSel, RegWEn, SysClk_t;
  wire [1:0] EX_MEM_WBSel, FWD_A, FWD_B, ID_EX_WBSel, MEM_WB_WBSel, WBSel;
  wire [2:0] EX_MEM_MemByteSel, ID_EX_MemByteSel, ImmSel, MemByteSel;
  wire [3:0] CSRCtl, EX_MEM_CSRCtl, ID_EX_CSRCtl;
  wire [4:0] ALUSel, BrSel, EX_MEM_rdi, EX_MEM_rs1, ID_EX_ALUSel, ID_EX_BrSel, ID_EX_rdi, ID_EX_rs1,
       ID_EX_rs2, MEM_WB_rdi, rdi, rs1, rs2;
  wire [6:0] op_code;
  wire [11:0] CSRAddr, EX_MEM_CSRAddr, ID_EX_CSRAddr;
  wire [31:0] ALUOut, CSR_cycle, CSR_test0, CSR_test1, CSR_time, CSROut, DMemOut, EX_MEM_PC, EX_MEM_PC_4,
       EX_MEM_RDataA, EX_MEM_RDataB, EX_RDataA, EX_RDataB, ID_EX_Imm, ID_EX_PC, ID_EX_PC_4, ID_EX_RDataA,
       ID_EX_RDataB, IF_ID_Inst, IF_ID_PC, IF_ID_PC_4, ImmGenOut, Inst_t, InstOut, MEM_WB_ALUOut,
       MEM_WB_CSROut, MEM_WB_MemOut, MEM_WB_PC, MEM_WB_PC_4, MemOutAligned, MemOutData_t, PCPlus4, RDataA,
       RDataB, TEST_x31Data, WB_RegData;

  Clock clock_1 (.out(clock_1_out));
  Multiplexer multiplexer_1 (.in0(clock_1_out), .in1(SysClk), .out(SysClk_t), .sel(EXT_CTL_EN));
  // Probe on ALUOut
  // Probe on IMemPC
  // Probe on InstOut
  Multiplexer #(.width(32)) multiplexer_2 (.in0(InstOut), .in1(Inst), .out(Inst_t), .sel(EXT_CTL_EN));
  // Probe on Inst_t
  ProgramCounter programcounter_1 (
    .TargetAddr(ALUOut), .BranchCtl(PCSel), .PCWEn(PC_WE), .Clk(SysClk_t), .Reset(1'b0), .PcOut(IMemPC),
    .PcPlus4(PCPlus4));
  IMem imem_1 (.PC(IMemPC), .Inst(InstOut));
  assign TEST_Out = TEST_x31Data | CSR_test0;  // OR_Gate or_1, 32 bits wide
  // Probe on IF_ID_PC
  IF_ID if_id_1 (
    .Inst(Inst_t), .PC(IMemPC), .PCPlus4(PCPlus4), .IF_ID_WE(IF_ID_WE), .IF_ID_FLUSH(IF_ID_FLUSH),
    .SysClk(SysClk_t), .IF_ID_Inst(IF_ID_Inst), .IF_ID_PC(IF_ID_PC), .IF_ID_PC_4(IF_ID_PC_4),
    .IF_ID_valid(IF_ID_valid));
  // Probe on ImmGenOut
  // Probe on RDataA
  // Probe on RDataB
  // Probe on WB_RegData
  // Probe on MEM_WB_rdi
  // Probe on MEM_WB_RegWEn
  // Probe on MEM_WB_PC
  // MainController maincontroller_1: pin names not known; wires that end beside it: IF_ID_Inst, ImmSel, ASel, BSel, ALUSel, BrSel, MemRead, MemWrite, MemByteSel, RegWEn, WBSel, CSRAddr, CSRCtl, ecall, ebreak, rdi, rs1, rs2
  ImmGen immgen_1 (.InstIn(IF_ID_Inst), .ImmSelIn(ImmSel), .ImmOut(ImmGenOut));
  RegisterFile registerfile_1 (
    .Data(WB_RegData), .RdAddr(MEM_WB_rdi), .Rs1Addr(rs1), .Rs2Addr(rs2), .WriteEnable(MEM_WB_RegWEn),
    .Clk(SysClk_t), .DataA(RDataA), .DataB(RDataB), .TEST_x31Data(TEST_x31Data));
  // Probe on ImmSel
  // Probe on ASel
  // Probe on BSel
  // Probe on ALUSel
  // Probe on BrSel
  // Probe on MemRead
  // Probe on MemWrite
  // Probe on MemByteSel
  // Probe on RegWEn
  // Probe on WBSel
  // Probe on CSRAddr
  // Probe on CSRCtl
  // Probe on ecall
  // Probe on ebreak
  // Probe on rdi
  // Probe on rs1
  // Probe on rs2
  // Probe on op_code
  // Probe on ID_EX_PC
  ID_EX id_ex_1 (
    .RDataA(RDataA), .RDataB(RDataB), .Imm(ImmGenOut), .ASel(ASel), .BSel(BSel), .ALUSel(ALUSel),
    .BrSel(BrSel), .MemRead(MemRead), .MemWrite(MemWrite), .MemByteSel(MemByteSel), .RegWEn(RegWEn),
    .WBSel(WBSel), .CSRAddr(CSRAddr), .CSRCtl(CSRCtl), .ecall(ecall), .ebreak(ebreak), .rdi(rdi), .rs1(rs1),
    .rs2(rs2), .IF_ID_PC(IF_ID_PC), .IF_ID_PC_4(IF_ID_PC_4), .ID_EX_FLUSH(ID_EX_FLUSH),
    .IF_ID_valid(IF_ID_valid), .SysClk(SysClk_t), .ID_EX_RDataA(ID_EX_RDataA), .ID_EX_RDataB(ID_EX_RDataB),
    .ID_EX_Imm(ID_EX_Imm), .ID_EX_ASel(ID_EX_ASel), .ID_EX_BSel(ID_EX_BSel), .ID_EX_ALUSel(ID_EX_ALUSel),
    .ID_EX_BrSel(ID_EX_BrSel), .ID_EX_MemRead(ID_EX_MemRead), .ID_EX_MemWrite(ID_EX_MemWrite),
    .ID_EX_MemByteSel(ID_EX_MemByteSel), .ID_EX_RegWEn(ID_EX_RegWEn), .ID_EX_WBSel(ID_EX_WBSel),
    .ID_EX_CSRAddr(ID_EX_CSRAddr), .ID_EX_CSRCtl(ID_EX_CSRCtl), .ID_EX_ecall(ID_EX_ecall),
    .ID_EX_ebreak(ID_EX_ebreak), .ID_EX_rdi(ID_EX_rdi), .ID_EX_rs1(ID_EX_rs1), .ID_EX_rs2(ID_EX_rs2),
    .ID_EX_PC(ID_EX_PC), .ID_EX_PC_4(ID_EX_PC_4), .ID_EX_valid(ID_EX_valid));
  // Probe on ID_EX_RDataA
  // Probe on ID_EX_RDataB
  // Probe on ID_EX_Imm
  // Probe on ID_EX_ASel
  // Probe on ID_EX_BSel
  // Probe on ID_EX_ALUSel
  // Probe on ID_EX_BrSel
  // Probe on ID_EX_MemRead
  // Probe on ID_EX_MemWrite
  // Probe on ID_EX_MemByteSel
  // Probe on ID_EX_RegWEn
  // Probe on ID_EX_WBSel
  // Probe on ID_EX_CSRAddr
  // Probe on ID_EX_CSRCtl
  // Probe on ID_EX_ecall
  // Probe on ID_EX_ebreak
  // Probe on ID_EX_rdi
  // Probe on ID_EX_rs1
  // Probe on ID_EX_rs2
  // HazardControl hazardcontrol_1: pin names not known; wires that end beside it: PCSel, rs1, rs2, ID_EX_rs1, ID_EX_rs2, ID_EX_rdi, ID_EX_MemRead, ID_EX_RegWEn, ID_EX_CSRCtl, EX_MEM_rdi, EX_MEM_RegWEn, EX_MEM_CSRCtl, MEM_WB_rdi, PC_WE, IF_ID_WE, IF_ID_FLUSH, ID_EX_FLUSH, FWD_A, FWD_B
  // Probe on EX_RDataA
  // Probe on EX_RDataB
  // Probe on DMemAddr
  // Probe on WB_RegData
  // Probe on FWD_A
  // Probe on FWD_B
  // Probe on PCSel
  // Probe on ALUOut
  // Probe on PC_WE
  // Probe on IF_ID_WE
  // Probe on IF_ID_FLUSH
  // Probe on ID_EX_FLUSH
  // Probe on FWD_A
  // Probe on FWD_B
  ForwardControl forwardcontrol_1 (
    .ID_EX_RDataA(ID_EX_RDataA), .ID_EX_RDataB(ID_EX_RDataB), .EX_MEM_ALUOut(DMemAddr),
    .WB_RegData(WB_RegData), .FWD_A(FWD_A), .FWD_B(FWD_B), .RDataA(EX_RDataA), .RDataB(EX_RDataB));
  BranchController branchcontroller_1 (.DataA(EX_RDataA), .DataB(EX_RDataB), .BrSel(ID_EX_BrSel), .TakeBranch(PCSel));
  ALUControl alucontrol_1 (
    .RDataA(EX_RDataA), .PC(ID_EX_PC), .ASel(ID_EX_ASel), .RDataB(EX_RDataB), .ImmVal(ID_EX_Imm),
    .BSel(ID_EX_BSel), .ALUSel(ID_EX_ALUSel), .DataOut(ALUOut));
  // Probe on EX_MEM_PC
  EX_MEM ex_mem_1 (
    .ALUOut(ALUOut), .RDataB(EX_RDataB), .RDataA(EX_RDataA), .ID_EX_MemRead(ID_EX_MemRead),
    .ID_EX_MemWrite(ID_EX_MemWrite), .ID_EX_MemByteSel(ID_EX_MemByteSel), .ID_EX_RegWEn(ID_EX_RegWEn),
    .ID_EX_WBSel(ID_EX_WBSel), .ID_EX_CSRAddr(ID_EX_CSRAddr), .ID_EX_CSRCtl(ID_EX_CSRCtl),
    .ID_EX_ecall(ID_EX_ecall), .ID_EX_ebreak(ID_EX_ebreak), .ID_EX_rdi(ID_EX_rdi), .ID_EX_rs1(ID_EX_rs1),
    .ID_EX_PC(ID_EX_PC), .ID_EX_PC_4(ID_EX_PC_4), .ID_EX_valid(ID_EX_valid), .SysClk(SysClk_t),
    .EX_MEM_ALUOut(DMemAddr), .EX_MEM_RDataB(EX_MEM_RDataB), .EX_MEM_RDataA(EX_MEM_RDataA),
    .EX_MEM_MemRead(DMemRead), .EX_MEM_MemWrite(DMemWE), .EX_MEM_MemByteSel(EX_MEM_MemByteSel),
    .EX_MEM_RegWEn(EX_MEM_RegWEn), .EX_MEM_WBSel(EX_MEM_WBSel), .EX_MEM_CSRAddr(EX_MEM_CSRAddr),
    .EX_MEM_CSRCtl(EX_MEM_CSRCtl), .EX_MEM_ecall(EX_MEM_ecall), .EX_MEM_ebreak(EX_MEM_ebreak),
    .EX_MEM_rdi(EX_MEM_rdi), .EX_MEM_rs1(EX_MEM_rs1), .EX_MEM_PC(EX_MEM_PC), .EX_MEM_PC_4(EX_MEM_PC_4),
    .EX_MEM_valid(EX_MEM_valid));
  // Probe on DMemAddr
  // Probe on EX_MEM_RDataB
  // Probe on EX_MEM_RDataA
  // Probe on DMemRead
  // Probe on DMemWE
  // Probe on EX_MEM_MemByteSel
  // Probe on EX_MEM_RegWEn
  // Probe on EX_MEM_WBSel
  // Probe on EX_MEM_CSRAddr
  // Probe on EX_MEM_CSRCtl
  // Probe on EX_MEM_ecall
  // Probe on EX_MEM_ebreak
  // Probe on EX_MEM_rdi
  // Probe on EX_MEM_rs1
  // Probe on DMemWriteData
  // Probe on MemOutAligned
  // Probe on DMemOut
  Multiplexer #(.width(32)) multiplexer_3 (.in0(DMemOut), .in1(MemOutData), .out(MemOutData_t), .sel(EXT_CTL_EN));
  // Probe on MemOutData_t
  StoreAligner storealigner_1 (
    .MemAddr(DMemAddr), .Data(EX_MEM_RDataB), .ByteSel(EX_MEM_MemByteSel), .DataOut(DMemWriteData),
    .MaskOut(DMemMask));
  LoadAligner loadaligner_1 (
    .MemAddr(DMemAddr), .Data(MemOutData_t), .ByteSel(EX_MEM_MemByteSel), .Out0(MemOutAligned));
  DMem dmem_1 (
    .MemAddr(DMemAddr), .MemWrite(DMemWE), .MemRead(DMemRead), .StoreMast(DMemMask), .clk(SysClk_t),
    .WriteData(DMemWriteData), .MemOut(DMemOut));
  // CSR csr_1: pin names not known; wires that end beside it: EX_MEM_CSRAddr, EX_MEM_RDataA, EX_MEM_rdi, EX_MEM_rs1, MEM_WB_valid, EX_MEM_CSRCtl, SysClk_t, CSROut, CSR_test0, CSR_test1, CSR_cycle, TEST_instret, CSR_time
  // Probe on MEM_WB_PC
  MEM_WB mem_wb_1 (
    .MemData(MemOutAligned), .CSROut(CSROut), .EX_MEM_ALUOut(DMemAddr), .EX_MEM_RegWEn(EX_MEM_RegWEn),
    .EX_MEM_WBSel(EX_MEM_WBSel), .EX_MEM_ecall(EX_MEM_ecall), .EX_MEM_ebreak(EX_MEM_ebreak),
    .EX_MEM_rdi(EX_MEM_rdi), .EX_MEM_PC(EX_MEM_PC), .EX_MEM_PC_4(EX_MEM_PC_4), .EX_MEM_valid(EX_MEM_valid),
    .SysClk(SysClk_t), .MEM_WB_MemOut(MEM_WB_MemOut), .MEM_WB_CSROut(MEM_WB_CSROut),
    .MEM_WB_ALUOut(MEM_WB_ALUOut), .MEM_WB_RegWEn(MEM_WB_RegWEn), .MEM_WB_WBSel(MEM_WB_WBSel),
    .MEM_WB_ecall(MEM_WB_ecall), .MEM_WB_ebreak(MEM_WB_ebreak), .MEM_WB_rdi(MEM_WB_rdi),
    .MEM_WB_PC(MEM_WB_PC), .MEM_WB_PC_4(MEM_WB_PC_4), .MEM_WB_valid(MEM_WB_valid));
  // Probe on MEM_WB_MemOut
  // Probe on MEM_WB_CSROut
  // Probe on MEM_WB_ALUOut
  // Probe on MEM_WB_RegWEn
  // Probe on MEM_WB_WBSel
  // Probe on MEM_WB_ecall
  // Probe on MEM_WB_ebreak
  // Probe on MEM_WB_rdi
  // Probe on MEM_WB_PC
  // Probe on WB_RegData
  // WriteBackControl writebackcontrol_1: pin names not known; wires that end beside it: MEM_WB_ALUOut, MEM_WB_MemOut, MEM_WB_PC_4, MEM_WB_CSROut, MEM_WB_WBSel, WB_RegData

  // Other names for the same wires on the sheet: CSR_instret[31:0] = TEST_instret; EX_MEM_ALUOut[31:0] = DMemAddr;
  //   EX_MEM_MemRead = DMemRead; EX_MEM_MemWrite = DMemWE; EXT_Ctl = EXT_CTL_EN; EXT_HALT = HALT;
  //   EXT_Inst[31:0] = Inst; EXT_MemOutData[31:0] = MemOutData; EXT_SysClk = SysClk;
  //   MemWriteData[31:0] = DMemWriteData; PC[31:0] = IMemPC; StoreMask[3:0] = DMemMask

  // Notes on the sheet:
  //   Test Harness IO
  //   IF - Instruction Fetch
  //   Test IMem MUX
  //   IF_ID
  //   ID - Instruction Decode
  //   ID_EX
  //   EX - Execute
  //   EX_MEM
  //   Test DMem MUX
  //   MEM - Memory
  //   MEM_WB
  //   WB - Write Back
endmodule
