// Logisim project RiskVMemory.circ as structural Verilog: 9 circuits, main circuit RegisterFile
module RegisterFile (
  input  [31:0] Data,
  input  [4:0] RdAddr,
  input  [4:0] Rs1Addr,
  input  [4:0] Rs2Addr,
  input  WriteEnable,
  input  Clk,
  output [31:0] DataA,
  output [31:0] DataB,
  output [31:0] TEST_x31Data
);

  wire and_1_out, and_2_out, rd_not_zero, rs1_EQ_rdi, rs2_EQ_rdi, x1_we, x2_we, x3_we, x4_we, x5_we, x6_we,
       x7_we, x8_we, x9_we, x10_we, x11_we, x12_we, x13_we, x14_we, x15_we, x16_we, x17_we, x18_we, x19_we,
       x20_we, x21_we, x22_we, x23_we, x24_we, x25_we, x26_we, x27_we, x28_we, x29_we, x30_we, x31_we;
  wire [31:0] DataA_t, DataB_t, x1, x2, x3, x4, x5, x6, x7, x8, x9, x10, x11, x12, x13, x14, x15, x16, x17,
       x18, x19, x20, x21, x22, x23, x24, x25, x26, x27, x28, x29, x30;

  Demultiplexer #(.select(5)) demultiplexer_1 (
    .out1(x1_we), .out2(x2_we), .out3(x3_we), .out4(x4_we), .out5(x5_we), .out6(x6_we), .out7(x7_we),
    .out8(x8_we), .out9(x9_we), .out10(x10_we), .out11(x11_we), .out12(x12_we), .out13(x13_we),
    .out14(x14_we), .out15(x15_we), .out16(x16_we), .out17(x17_we), .out18(x18_we), .out19(x19_we),
    .out20(x20_we), .out21(x21_we), .out22(x22_we), .out23(x23_we), .out24(x24_we), .out25(x25_we),
    .out26(x26_we), .out27(x27_we), .out28(x28_we), .out29(x29_we), .out30(x30_we), .out31(x31_we),
    .in(WriteEnable), .sel(RdAddr));  // open: out0
  Register #(.width(32)) register_1 (.D(Data), .en(x1_we), .clk(Clk), .Q(x1));  // open: clr
  Register #(.width(32)) register_2 (.D(Data), .en(x2_we), .clk(Clk), .Q(x2));  // open: clr
  Register #(.width(32)) register_3 (.D(Data), .en(x3_we), .clk(Clk), .Q(x3));  // open: clr
  Register #(.width(32)) register_4 (.D(Data), .en(x4_we), .clk(Clk), .Q(x4));  // open: clr
  Register #(.width(32)) register_5 (.D(Data), .en(x5_we), .clk(Clk), .Q(x5));  // open: clr
  Register #(.width(32)) register_6 (.D(Data), .en(x6_we), .clk(Clk), .Q(x6));  // open: clr
  Register #(.width(32)) register_7 (.D(Data), .en(x7_we), .clk(Clk), .Q(x7));  // open: clr
  Register #(.width(32)) register_8 (.D(Data), .en(x8_we), .clk(Clk), .Q(x8));  // open: clr
  Register #(.width(32)) register_9 (.D(Data), .en(x9_we), .clk(Clk), .Q(x9));  // open: clr
  Register #(.width(32)) register_10 (.D(Data), .en(x10_we), .clk(Clk), .Q(x10));  // open: clr
  Register #(.width(32)) register_11 (.D(Data), .en(x11_we), .clk(Clk), .Q(x11));  // open: clr
  Register #(.width(32)) register_12 (.D(Data), .en(x12_we), .clk(Clk), .Q(x12));  // open: clr
  Register #(.width(32)) register_13 (.D(Data), .en(x13_we), .clk(Clk), .Q(x13));  // open: clr
  Register #(.width(32)) register_14 (.D(Data), .en(x14_we), .clk(Clk), .Q(x14));  // open: clr
  Register #(.width(32)) register_15 (.D(Data), .en(x15_we), .clk(Clk), .Q(x15));  // open: clr
  Register #(.width(32)) register_16 (.D(Data), .en(x16_we), .clk(Clk), .Q(x16));  // open: clr
  Register #(.width(32)) register_17 (.D(Data), .en(x17_we), .clk(Clk), .Q(x17));  // open: clr
  Register #(.width(32)) register_18 (.D(Data), .en(x18_we), .clk(Clk), .Q(x18));  // open: clr
  Register #(.width(32)) register_19 (.D(Data), .en(x19_we), .clk(Clk), .Q(x19));  // open: clr
  Register #(.width(32)) register_20 (.D(Data), .en(x20_we), .clk(Clk), .Q(x20));  // open: clr
  Register #(.width(32)) register_21 (.D(Data), .en(x21_we), .clk(Clk), .Q(x21));  // open: clr
  Register #(.width(32)) register_22 (.D(Data), .en(x22_we), .clk(Clk), .Q(x22));  // open: clr
  Register #(.width(32)) register_23 (.D(Data), .en(x23_we), .clk(Clk), .Q(x23));  // open: clr
  Register #(.width(32)) register_24 (.D(Data), .en(x24_we), .clk(Clk), .Q(x24));  // open: clr
  Register #(.width(32)) register_25 (.D(Data), .en(x25_we), .clk(Clk), .Q(x25));  // open: clr
  Register #(.width(32)) register_26 (.D(Data), .en(x26_we), .clk(Clk), .Q(x26));  // open: clr
  Register #(.width(32)) register_27 (.D(Data), .en(x27_we), .clk(Clk), .Q(x27));  // open: clr
  Register #(.width(32)) register_28 (.D(Data), .en(x28_we), .clk(Clk), .Q(x28));  // open: clr
  Register #(.width(32)) register_29 (.D(Data), .en(x29_we), .clk(Clk), .Q(x29));  // open: clr
  Register #(.width(32)) register_30 (.D(Data), .en(x30_we), .clk(Clk), .Q(x30));  // open: clr
  Register #(.width(32)) register_31 (.D(Data), .en(x31_we), .clk(Clk), .Q(TEST_x31Data));  // open: clr
  Multiplexer #(.select(5), .width(32)) multiplexer_1 (
    .in0({32{1'b0}}), .in1(x1), .in2(x2), .in3(x3), .in4(x4), .in5(x5), .in6(x6), .in7(x7), .in8(x8),
    .in9(x9), .in10(x10), .in11(x11), .in12(x12), .in13(x13), .in14(x14), .in15(x15), .in16(x16), .in17(x17),
    .in18(x18), .in19(x19), .in20(x20), .in21(x21), .in22(x22), .in23(x23), .in24(x24), .in25(x25),
    .in26(x26), .in27(x27), .in28(x28), .in29(x29), .in30(x30), .in31(TEST_x31Data), .out(DataA_t),
    .sel(Rs1Addr));
  Multiplexer #(.select(5), .width(32)) multiplexer_2 (
    .in0({32{1'b0}}), .in1(x1), .in2(x2), .in3(x3), .in4(x4), .in5(x5), .in6(x6), .in7(x7), .in8(x8),
    .in9(x9), .in10(x10), .in11(x11), .in12(x12), .in13(x13), .in14(x14), .in15(x15), .in16(x16), .in17(x17),
    .in18(x18), .in19(x19), .in20(x20), .in21(x21), .in22(x22), .in23(x23), .in24(x24), .in25(x25),
    .in26(x26), .in27(x27), .in28(x28), .in29(x29), .in30(x30), .in31(TEST_x31Data), .out(DataB_t),
    .sel(Rs2Addr));
  RegXORComparitor regxorcomparitor_1 (.A(Rs1Addr), .B(RdAddr), .EQ(rs1_EQ_rdi));
  Multiplexer #(.width(32)) multiplexer_3 (.in0(DataA_t), .in1(Data), .out(DataA), .sel(and_1_out));
  and and_1 (and_1_out, rs1_EQ_rdi, WriteEnable, rd_not_zero);
  RegXORComparitor regxorcomparitor_2 (.A(Rs2Addr), .B(RdAddr), .EQ(rs2_EQ_rdi));
  Multiplexer #(.width(32)) multiplexer_4 (.in0(DataB_t), .in1(Data), .out(DataB), .sel(and_2_out));
  and and_2 (and_2_out, rs2_EQ_rdi, WriteEnable, rd_not_zero);
  or or_1 (rd_not_zero, RdAddr[0], RdAddr[1], RdAddr[2], RdAddr[3], RdAddr[4]);

  // Other names for the same wires on the sheet: DataAOut[31:0] = DataA; DataBOut[31:0] = DataB; rd[4:0] = RdAddr;
  //   rs1[4:0] = Rs1Addr; rs2[4:0] = Rs2Addr; we_in = WriteEnable; x31[31:0] = TEST_x31Data

  // Notes on the sheet:
  //   Write-Back to Decode RAW Data Hazard.
  //   Expose x31 for test results
endmodule

module LoadAligner (
  input  [31:0] MemAddr,
  input  [31:0] Data,
  input  [2:0] ByteSel,
  output [31:0] Out0
);

  wire and_3_out, B, missAlign;
  wire [4:3] shamt;
  wire [31:0] lb, lbu, lh, lhu, shiftedData;

  // Probe on Data
  // Probe on ByteSel
  // Probe on MemAddr[1:0]
  // Probe on MemAddr
  and and_1 (B, ~ByteSel[1], ~ByteSel[2]);  // AND_Gate
  and and_2 (missAlign, MemAddr[0], ~MemAddr[1], ByteSel[1], ~ByteSel[2]);  // AND_Gate
  and and_3 (and_3_out, ~MemAddr[0], B, ~ByteSel[2]);  // AND_Gate
  or or_1 (shamt[3], and_3_out, missAlign);
  and and_4 (shamt[4], ~MemAddr[1], ~ByteSel[2], ~missAlign);  // AND_Gate
  Shifter #(.shift("lr"), .width(32)) shifter_1 (.in(Data), .\dist ({shamt, 3'b000}), .out(shiftedData));
  // Probe on {shamt, 3'b000}
  // Probe on shiftedData
  assign lb = {{24{shiftedData[7]}}, shiftedData[7:0]};  // Bit_Extender bit_extender_1
  assign lbu = {{24{1'b0}}, shiftedData[7:0]};  // Bit_Extender bit_extender_2
  assign lh = {{16{shiftedData[15]}}, shiftedData[15:0]};  // Bit_Extender bit_extender_3
  assign lhu = {{16{1'b0}}, shiftedData[15:0]};  // Bit_Extender bit_extender_4
  Multiplexer #(.select(3), .width(32)) multiplexer_1 (
    .in0(lb), .in1(lbu), .in2(lh), .in3(lhu), .in4(Data), .out(Out0), .sel(ByteSel));  // open: in5, in6, in7
  // Probe on ByteSel

  // Other names for the same wires on the sheet: H = ByteSel[1]; W = ByteSel[2]; dataIn[31:0] = Data;
  //   AddrOffset[1:0] = MemAddr[1:0]; offset0 = MemAddr[0]; offset1 = MemAddr[1]

  // Notes on the sheet:
  //   Signed Byte = 000
  //   Unsigned Byte = 001
  //   Signed Half Word = 010
  //   Unsigned Half Word = 011
  //   Full Word = 100
  //   Shift data by address offset amount
endmodule

module StoreMaskGenerator (
  input  [1:0] AddrOffset,
  input  [2:0] ByteSel,
  output [3:0] OutMask
);

  wire A0_AND_B, A0_OR_H, A1_AND_NOT_A0_AND_B, A1_XOR_A0, and_5_out, and_6_out, and_7_out, and_8_out,
       and_9_out, B, B_OR_H, NOT_A0, NOT_A0_AND_H, NOT_A1, or_3_out, or_4_out, or_5_out;

  not not_1 (NOT_A0, AddrOffset[0]);
  not not_2 (NOT_A1, AddrOffset[1]);
  and and_1 (B, ~ByteSel[1], ~ByteSel[2]);  // AND_Gate
  and and_2 (NOT_A0_AND_H, NOT_A0, ByteSel[1]);
  and and_3 (A0_AND_B, AddrOffset[0], B);
  or or_1 (B_OR_H, B, ByteSel[1]);
  and and_4 (A1_AND_NOT_A0_AND_B, AddrOffset[1], NOT_A0, B);
  xor xor_1 (A1_XOR_A0, AddrOffset[1], AddrOffset[0]);
  or or_2 (A0_OR_H, ByteSel[1], AddrOffset[0]);
  and and_5 (and_5_out, AddrOffset[1], or_3_out);
  or or_3 (or_3_out, A0_AND_B, ByteSel[1]);
  and and_6 (and_6_out, A1_XOR_A0, ByteSel[1]);
  and and_7 (and_7_out, NOT_A1, or_4_out);
  or or_4 (or_4_out, NOT_A0_AND_H, A0_AND_B);
  and and_8 (and_8_out, NOT_A1, and_9_out);
  and and_9 (and_9_out, NOT_A0, B_OR_H);
  or or_5 (or_5_out, A1_AND_NOT_A0_AND_B, and_6_out);
  or or_6 (OutMask[1], or_5_out, ByteSel[2]);
  or or_7 (OutMask[3], and_8_out, ByteSel[2]);
  or or_8 (OutMask[0], and_5_out, ByteSel[2]);
  or or_9 (OutMask[2], and_7_out, A0_OR_H, ByteSel[2]);

  // Other names for the same wires on the sheet: A0 = AddrOffset[0]; A1 = AddrOffset[1]; H = ByteSel[1];
  //   W = ByteSel[2]

  // Notes on the sheet:
  //   Mask[0] = W OR (A1 AND (A0 AND B OR H))
  //   Mask[1] = W OR (A1 AND ~A0 AND B) OR (H AND (A1 XOR A0))
  //   Mask[2] = W OR (~A1 AND (A0 AND B OR ~A0 AND H))
  //   Mask[3] = W OR (~A1 AND (~A0 AND B OR H))
endmodule

module StoreAligner (
  input  [31:0] MemAddr,
  input  [31:0] Data,
  input  [2:0] ByteSel,
  output [31:0] DataOut,
  output [3:0] MaskOut
);

  wire and_3_out, B, missAlign;
  wire [4:3] shamt;

  // Probe on MemAddr[1:0]
  // Probe on MemAddr
  // Probe on Data
  // Probe on ByteSel
  and and_1 (B, ~ByteSel[1], ~ByteSel[2]);  // AND_Gate
  and and_2 (missAlign, MemAddr[0], ~MemAddr[1], ByteSel[1], ~ByteSel[2]);  // AND_Gate
  and and_3 (and_3_out, ~MemAddr[0], B, ~ByteSel[2]);  // AND_Gate
  or or_1 (shamt[3], and_3_out, missAlign);
  and and_4 (shamt[4], ~MemAddr[1], ~ByteSel[2], ~missAlign);  // AND_Gate
  // Probe on MaskOut
  StoreMaskGenerator storemaskgenerator_1 (.AddrOffset(MemAddr[1:0]), .ByteSel(ByteSel), .OutMask(MaskOut));
  // Probe on {shamt, 3'b000}
  // Probe on DataOut
  Shifter #(.width(32)) shifter_1 (.in(Data), .\dist ({shamt, 3'b000}), .out(DataOut));

  // Other names for the same wires on the sheet: dataIn[31:0] = Data; AddrOffset[1:0] = MemAddr[1:0];
  //   offset0 = MemAddr[0]; offset1 = MemAddr[1]; MemByteSel[2:0] = ByteSel; H = ByteSel[1]; W = ByteSel[2];
  //   shiftedData[31:0] = DataOut; StoreMask[3:0] = MaskOut

  // Notes on the sheet:
  //   Shift data by address offset amount
endmodule

module IMem (
  input  [31:0] PC,
  output [31:0] Inst
);

  // Probe on PC
  ROM #(.addrWidth(10), .dataWidth(32)) IMem (.addr(PC[11:2]), .data(Inst));
  // Probe on Inst

  // Notes on the sheet:
  //   contents of IMem (hex, n*v repeats v):
  //   93 113 193 213 293 4000093 2a00113 20a023 4000093 a183 2219a63 a00213 1400293 1013 26313 500213
  //   500293 520463 140006f 0 0 100f93 6f fff00f93 ffdff06f
endmodule

module DMem (
  input  [31:0] MemAddr,
  input  MemWrite,
  input  MemRead,
  input  [3:0] StoreMast,
  input  clk,
  input  [31:0] WriteData,
  output [31:0] MemOut
);

  // Probe on MemAddr
  RAM #(.addrWidth(10), .asyncread("true"), .byteenables("byteEnables"), .dataWidth(32)) DMem (
    .addr(MemAddr[11:2]), .we(MemWrite), .oe(MemRead), .clk(clk), .din(WriteData), .dout(MemOut),
    .be3(StoreMast[3]), .be2(StoreMast[2]), .be1(StoreMast[1]), .be0(StoreMast[0]));
  // Probe on WriteData
  // Probe on MemOut

  // Other names for the same wires on the sheet: AddrOffset[1:0] = MemAddr[1:0]; MemWriteData[31:0] = WriteData;
  //   StoreMask[3:0] = StoreMast; SysClk = clk

  // Notes on the sheet:
  //   MEM - Memory
endmodule

module RegXORComparitor (
  input  [4:0] A,
  input  [4:0] B,
  output EQ
);

  wire [4:0] xor_1_out;

  assign xor_1_out = A ^ B;  // XOR_Gate xor_1, 5 bits wide
  and and_1 (EQ, ~xor_1_out[0], ~xor_1_out[1], ~xor_1_out[2], ~xor_1_out[3], ~xor_1_out[4]);  // AND_Gate
endmodule

module CSR (
  input  [11:0] CSRAddr,
  input  [31:0] RDataA,
  input  [4:0] rdi,
  input  [4:0] uimm,
  input  inst_valid,
  input  [3:0] CSRCtl,
  input  clk,
  output [31:0] DataOut
);

  wire csraddreq_1_eq, csraddreq_2_eq, csraddreq_3_eq, csraddreq_4_eq, is_cycle_addr, is_instret_addr,
       is_rdi_zero, is_source_zero, is_uimm_zero, nand_1_out, WE;
  wire [31:0] and_3_out, bit_extender_1_out, cycle_inc, cycle_out, DataIn, instret_inc, instret_out,
       multiplexer_4_out, multiplexer_5_out, multiplexer_6_out, NewData, or_1_out;

  and and_1 (is_rdi_zero, ~rdi[0], ~rdi[1], ~rdi[2], ~rdi[3], ~rdi[4]);  // AND_Gate
  and and_2 (is_uimm_zero, ~uimm[0], ~uimm[1], ~uimm[2], ~uimm[3], ~uimm[4]);  // AND_Gate
  Multiplexer multiplexer_1 (.in0(is_rdi_zero), .in1(is_uimm_zero), .out(is_source_zero), .sel(CSRCtl[2]));
  assign bit_extender_1_out = {{27{1'b0}}, uimm};  // Bit_Extender bit_extender_1
  assign or_1_out = DataIn | DataOut;  // OR_Gate or_1, 32 bits wide
  assign and_3_out = ~DataIn & DataOut;  // AND_Gate and_3, 32 bits wide
  Multiplexer #(.width(32)) multiplexer_2 (.in0(RDataA), .in1(bit_extender_1_out), .out(DataIn), .sel(CSRCtl[2]));
  Multiplexer #(.select(2), .width(32)) multiplexer_3 (
    .in1(DataIn), .in2(or_1_out), .in3(and_3_out), .out(NewData), .sel(CSRCtl[1:0]));  // open: in0
  nand nand_1 (nand_1_out, CSRCtl[1], is_source_zero);
  and and_4 (WE, nand_1_out, CSRCtl[3]);
  Multiplexer #(.width(32)) multiplexer_4 (.in0({32{1'b0}}), .in1(32'h1), .out(multiplexer_4_out), .sel(inst_valid));
  CSRAddrEQ csraddreq_1 (.A(CSRAddr), .B(12'hc00), .EQ(csraddreq_1_eq));
  CSRAddrEQ csraddreq_2 (.A(CSRAddr), .B(12'h300), .EQ(csraddreq_2_eq));
  Multiplexer #(.width(32)) multiplexer_5 (
    .in0(cycle_inc), .in1(NewData), .out(multiplexer_5_out), .sel(is_cycle_addr));
  Adder #(.width(32)) adder_1 (.a(32'h1), .b(cycle_out), .out(cycle_inc));  // open: cin, cout
  or or_2 (is_cycle_addr, csraddreq_1_eq, csraddreq_2_eq);
  Register #(.width(32)) register_1 (.D(multiplexer_5_out), .en(1'b1), .clk(clk), .Q(cycle_out));  // open: clr
  CSRAddrEQ csraddreq_3 (.A(CSRAddr), .B(12'hc02), .EQ(csraddreq_3_eq));
  CSRAddrEQ csraddreq_4 (.A(CSRAddr), .B(12'h302), .EQ(csraddreq_4_eq));
  Register #(.width(32)) register_2 (.D(multiplexer_6_out), .en(1'b1), .clk(clk), .Q(instret_out));  // open: clr
  Multiplexer #(.width(32)) multiplexer_6 (
    .in0(instret_inc), .in1(NewData), .out(multiplexer_6_out), .sel(is_instret_addr));
  Adder #(.width(32)) adder_2 (.a(multiplexer_4_out), .b(instret_out), .out(instret_inc));  // open: cin, cout
  or or_3 (is_instret_addr, csraddreq_3_eq, csraddreq_4_eq);
  RAM #(.addrWidth(12), .dataWidth(32)) ram_1 (
    .addr(CSRAddr), .we(WE), .oe(1'b1), .clk(clk), .din(NewData), .dout(DataOut));

  // Other names for the same wires on the sheet: csr_op[1:0] = CSRCtl[1:0]; is_clear_or_set = CSRCtl[1];
  //   is_csr_uimm = CSRCtl[2]; is_csr_active = CSRCtl[3]

  // Notes on the sheet:
  //   default incremented value if valid
  //   cycle
  //   instret
  //   write value if incoming address matches instret
endmodule

module CSRAddrEQ (
  input  [11:0] A,
  input  [11:0] B,
  output EQ
);

  wire [11:0] xor_1_out;

  assign xor_1_out = A ^ B;  // XOR_Gate xor_1, 12 bits wide
  and and_1 (EQ, ~xor_1_out[0], ~xor_1_out[1], ~xor_1_out[2], ~xor_1_out[3], ~xor_1_out[4], ~xor_1_out[5], ~xor_1_out[6], ~xor_1_out[7], ~xor_1_out[8], ~xor_1_out[9], ~xor_1_out[10], ~xor_1_out[11]);  // AND_Gate
endmodule
