// Logisim project RiskVPipelineRegs.circ as structural Verilog: 9 circuits, main circuit PipelineReg32Bit
module PipelineReg32Bit (
  input  [31:0] DataIn,
  input  WE,
  input  FLUSH,
  input  clk,
  output [31:0] DataOut
);

  wire or_1_out;
  wire [31:0] multiplexer_1_out;

  // Probe on multiplexer_1_out
  Multiplexer #(.width(32)) multiplexer_1 (.in0(DataIn), .in1({32{1'b0}}), .out(multiplexer_1_out), .sel(FLUSH));
  or or_1 (or_1_out, WE, FLUSH);
  Register #(.width(32)) register_1 (.D(multiplexer_1_out), .en(or_1_out), .clk(clk), .Q(DataOut));  // open: clr
  // Probe on DataOut

  // Other names for the same wires on the sheet: data[31:0] = DataIn
endmodule

module PipelineReg5Bit (
  input  [4:0] DataIn,
  input  WE,
  input  FLUSH,
  input  clk,
  output [4:0] DataOut
);

  wire or_1_out;
  wire [4:0] multiplexer_1_out;

  // Probe on multiplexer_1_out
  Multiplexer #(.width(5)) multiplexer_1 (.in0(DataIn), .in1({5{1'b0}}), .out(multiplexer_1_out), .sel(FLUSH));
  or or_1 (or_1_out, WE, FLUSH);
  Register #(.width(5)) register_1 (.D(multiplexer_1_out), .en(or_1_out), .clk(clk), .Q(DataOut));  // open: clr
  // Probe on DataOut

  // Other names for the same wires on the sheet: data[4:0] = DataIn
endmodule

module PipelineReg1Bit (
  input  DataIn,
  input  WE,
  input  FLUSH,
  input  clk,
  output DataOut
);

  wire multiplexer_1_out, or_1_out;

  // Probe on multiplexer_1_out
  Multiplexer multiplexer_1 (.in0(DataIn), .in1(1'b0), .out(multiplexer_1_out), .sel(FLUSH));
  or or_1 (or_1_out, WE, FLUSH);
  Register #(.width(1)) register_1 (.D(multiplexer_1_out), .en(or_1_out), .clk(clk), .Q(DataOut));  // open: clr
  // Probe on DataOut

  // Other names for the same wires on the sheet: data = DataIn
endmodule

module PipelineReg3Bit (
  input  [2:0] DataIn,
  input  WE,
  input  FLUSH,
  input  clk,
  output [2:0] DataOut
);

  wire or_1_out;
  wire [2:0] multiplexer_1_out;

  // Probe on multiplexer_1_out
  Multiplexer #(.width(3)) multiplexer_1 (.in0(DataIn), .in1(3'b000), .out(multiplexer_1_out), .sel(FLUSH));
  or or_1 (or_1_out, WE, FLUSH);
  Register #(.width(3)) register_1 (.D(multiplexer_1_out), .en(or_1_out), .clk(clk), .Q(DataOut));  // open: clr
  // Probe on DataOut

  // Other names for the same wires on the sheet: data[2:0] = DataIn
endmodule

module PipelineReg2Bit (
  input  [1:0] DataIn,
  input  WE,
  input  FLUSH,
  input  clk,
  output [1:0] DataOut
);

  wire or_1_out;
  wire [1:0] multiplexer_1_out;

  // Probe on multiplexer_1_out
  Multiplexer #(.width(2)) multiplexer_1 (.in0(DataIn), .in1(2'b00), .out(multiplexer_1_out), .sel(FLUSH));
  or or_1 (or_1_out, WE, FLUSH);
  Register #(.width(2)) register_1 (.D(multiplexer_1_out), .en(or_1_out), .clk(clk), .Q(DataOut));  // open: clr
  // Probe on DataOut

  // Other names for the same wires on the sheet: data[1:0] = DataIn
endmodule

module IF_ID (
  input  [31:0] Inst,
  input  [31:0] PC,
  input  [31:0] PCPlus4,
  input  IF_ID_WE,
  input  IF_ID_FLUSH,
  input  SysClk,
  output [31:0] IF_ID_Inst,
  output [31:0] IF_ID_PC,
  output [31:0] IF_ID_PC_4
);

  PipelineReg32Bit ID_ID_INST (.DataIn(Inst), .WE(IF_ID_WE), .FLUSH(IF_ID_FLUSH), .clk(SysClk), .DataOut(IF_ID_Inst));
  PipelineReg32Bit pipelinereg32bit_1 (.DataIn(PC), .WE(IF_ID_WE), .clk(SysClk), .DataOut(IF_ID_PC));  // open: FLUSH
  PipelineReg32Bit pipelinereg32bit_2 (
    .DataIn(PCPlus4), .WE(IF_ID_WE), .clk(SysClk), .DataOut(IF_ID_PC_4));  // open: FLUSH

  // Notes on the sheet:
  //   IF_ID
endmodule

module ID_EX (
  input  [31:0] RDataA,
  input  [31:0] RDataB,
  input  [31:0] Imm,
  input  ASel,
  input  BSel,
  input  [31:0] ID_EX_RDataA,
  input  [31:0] ID_EX_RDataB,
  input  [4:0] ALUSel,
  input  [31:0] ID_EX_Imm,
  input  [4:0] BrSel,
  input  ID_EX_ASel,
  input  MemRead,
  input  ID_EX_BSel,
  input  MemWrite,
  input  [2:0] MemByteSel,
  input  [4:0] ID_EX_ALUSel,
  input  [4:0] ID_EX_BrSel,
  input  RegWEn,
  input  ID_EX_MemRead,
  input  [1:0] WBSel,
  input  ID_EX_MemWrite,
  input  ecall,
  input  [2:0] ID_EX_MemByteSel,
  input  ebreak,
  input  ID_EX_RegWEn,
  input  [4:0] rdi,
  input  [1:0] ID_EX_WBSel,
  input  [4:0] rs1,
  input  ID_EX_ecall,
  input  [4:0] rs2,
  input  ID_EX_ebreak,
  input  [31:0] IF_ID_PC,
  input  [4:0] ID_EX_rdi,
  input  [31:0] IF_ID_PC_4,
  input  [4:0] ID_EX_rs1,
  input  [4:0] ID_EX_rs2,
  input  in_37,
  input  [31:0] ID_EX_PC,
  input  in_39,
  input  [31:0] ID_EX_PC_4
);

  PipelineReg32Bit pipelinereg32bit_1 (.DataIn(RDataA), .WE(1'b1), .FLUSH(in_37), .clk(in_39), .DataOut(ID_EX_RDataA));
  PipelineReg32Bit pipelinereg32bit_2 (.DataIn(RDataB), .WE(1'b1), .FLUSH(in_37), .clk(in_39), .DataOut(ID_EX_RDataB));
  PipelineReg32Bit pipelinereg32bit_3 (.DataIn(Imm), .WE(1'b1), .FLUSH(in_37), .clk(in_39), .DataOut(ID_EX_Imm));
  PipelineReg1Bit pipelinereg1bit_1 (.DataIn(ASel), .WE(1'b1), .FLUSH(in_37), .clk(in_39), .DataOut(ID_EX_ASel));
  PipelineReg1Bit pipelinereg1bit_2 (.DataIn(BSel), .WE(1'b1), .FLUSH(in_37), .clk(in_39), .DataOut(ID_EX_BSel));
  PipelineReg5Bit pipelinereg5bit_1 (.DataIn(ALUSel), .WE(1'b1), .FLUSH(in_37), .clk(in_39), .DataOut(ID_EX_ALUSel));
  PipelineReg5Bit pipelinereg5bit_2 (.DataIn(BrSel), .WE(1'b1), .FLUSH(in_37), .clk(in_39), .DataOut(ID_EX_BrSel));
  PipelineReg1Bit pipelinereg1bit_3 (.DataIn(MemRead), .WE(1'b1), .FLUSH(in_37), .clk(in_39), .DataOut(ID_EX_MemRead));
  PipelineReg1Bit pipelinereg1bit_4 (
    .DataIn(MemWrite), .WE(1'b1), .FLUSH(in_37), .clk(in_39), .DataOut(ID_EX_MemWrite));
  PipelineReg3Bit pipelinereg3bit_1 (
    .DataIn(MemByteSel), .WE(1'b1), .FLUSH(in_37), .clk(in_39), .DataOut(ID_EX_MemByteSel));
  PipelineReg1Bit pipelinereg1bit_5 (.DataIn(RegWEn), .WE(1'b1), .FLUSH(in_37), .clk(in_39), .DataOut(ID_EX_RegWEn));
  PipelineReg2Bit pipelinereg2bit_1 (.DataIn(WBSel), .WE(1'b1), .FLUSH(in_37), .clk(in_39), .DataOut(ID_EX_WBSel));
  PipelineReg1Bit pipelinereg1bit_6 (.DataIn(ecall), .WE(1'b1), .FLUSH(in_37), .clk(in_39), .DataOut(ID_EX_ecall));
  PipelineReg1Bit pipelinereg1bit_7 (.DataIn(ebreak), .WE(1'b1), .FLUSH(in_37), .clk(in_39), .DataOut(ID_EX_ebreak));
  PipelineReg5Bit pipelinereg5bit_3 (.DataIn(rdi), .WE(1'b1), .FLUSH(in_37), .clk(in_39), .DataOut(ID_EX_rdi));
  PipelineReg5Bit pipelinereg5bit_4 (.DataIn(rs1), .WE(1'b1), .FLUSH(in_37), .clk(in_39), .DataOut(ID_EX_rs1));
  PipelineReg5Bit pipelinereg5bit_5 (.DataIn(rs2), .WE(1'b1), .FLUSH(in_37), .clk(in_39), .DataOut(ID_EX_rs2));
  PipelineReg32Bit pipelinereg32bit_4 (.DataIn(IF_ID_PC), .WE(1'b1), .clk(in_39), .DataOut(ID_EX_PC));  // open: FLUSH
  PipelineReg32Bit pipelinereg32bit_5 (
    .DataIn(IF_ID_PC_4), .WE(1'b1), .clk(in_39), .DataOut(ID_EX_PC_4));  // open: FLUSH

  // Other names for the same wires on the sheet: ID_EX_FLUSH = in_37; SysClk = in_39

  // Notes on the sheet:
  //   ID_EX
endmodule

module EX_MEM (
  input  [31:0] ALUOut,
  input  [31:0] ID_EX_RDataB,
  input  ID_EX_MemRead,
  input  ID_EX_MemWrite,
  input  [2:0] ID_EX_MemByteSel,
  input  ID_EX_RegWEn,
  input  [1:0] ID_EX_WBSel,
  input  ID_EX_ecall,
  input  ID_EX_ebreak,
  input  [4:0] ID_EX_rdi,
  input  [31:0] ID_EX_PC,
  input  [31:0] ID_EX_PC_4,
  input  in_13,
  output [31:0] EX_MEM_ALUOut,
  output [31:0] EX_MEM_RDataB,
  output EX_MEM_MemRead,
  output EX_MEM_MemWrite,
  output [2:0] EX_MEM_MemByteSel,
  output EX_MEM_RegWEn,
  output [1:0] EX_MEM_WBSel,
  output EX_MEM_ecall,
  output EX_MEM_ebreak,
  output [4:0] EX_MEM_rdi,
  output [31:0] EX_MEM_PC,
  output [31:0] EX_MEM_PC_4
);

  PipelineReg32Bit pipelinereg32bit_1 (.DataIn(ALUOut), .WE(1'b1), .FLUSH(1'b0), .clk(in_13), .DataOut(EX_MEM_ALUOut));
  PipelineReg32Bit pipelinereg32bit_2 (
    .DataIn(ID_EX_RDataB), .WE(1'b1), .FLUSH(1'b0), .clk(in_13), .DataOut(EX_MEM_RDataB));
  PipelineReg1Bit pipelinereg1bit_1 (
    .DataIn(ID_EX_MemRead), .WE(1'b1), .FLUSH(1'b0), .clk(in_13), .DataOut(EX_MEM_MemRead));
  PipelineReg1Bit pipelinereg1bit_2 (
    .DataIn(ID_EX_MemWrite), .WE(1'b1), .FLUSH(1'b0), .clk(in_13), .DataOut(EX_MEM_MemWrite));
  PipelineReg3Bit pipelinereg3bit_1 (
    .DataIn(ID_EX_MemByteSel), .WE(1'b1), .FLUSH(1'b0), .clk(in_13), .DataOut(EX_MEM_MemByteSel));
  PipelineReg1Bit pipelinereg1bit_3 (
    .DataIn(ID_EX_RegWEn), .WE(1'b1), .FLUSH(1'b0), .clk(in_13), .DataOut(EX_MEM_RegWEn));
  PipelineReg2Bit pipelinereg2bit_1 (
    .DataIn(ID_EX_WBSel), .WE(1'b1), .FLUSH(1'b0), .clk(in_13), .DataOut(EX_MEM_WBSel));
  PipelineReg1Bit pipelinereg1bit_4 (
    .DataIn(ID_EX_ecall), .WE(1'b1), .FLUSH(1'b0), .clk(in_13), .DataOut(EX_MEM_ecall));
  PipelineReg1Bit pipelinereg1bit_5 (
    .DataIn(ID_EX_ebreak), .WE(1'b1), .FLUSH(1'b0), .clk(in_13), .DataOut(EX_MEM_ebreak));
  PipelineReg5Bit pipelinereg5bit_1 (.DataIn(ID_EX_rdi), .WE(1'b1), .FLUSH(1'b0), .clk(in_13), .DataOut(EX_MEM_rdi));
  PipelineReg32Bit pipelinereg32bit_3 (.DataIn(ID_EX_PC), .WE(1'b1), .clk(in_13), .DataOut(EX_MEM_PC));  // open: FLUSH
  PipelineReg32Bit pipelinereg32bit_4 (
    .DataIn(ID_EX_PC_4), .WE(1'b1), .clk(in_13), .DataOut(EX_MEM_PC_4));  // open: FLUSH

  // Other names for the same wires on the sheet: SysClk = in_13
endmodule

module MEM_WB (
  input  [31:0] MemData,
  input  [31:0] EX_MEM_ALUOut,
  input  [31:0] MEM_WB_MemOut,
  input  EX_MEM_RegWEn,
  input  [31:0] MEM_WB_ALUOut,
  input  [1:0] EX_MEM_WBSel,
  input  MEM_WB_RegWEn,
  input  EX_MEM_ecall,
  input  [1:0] MEM_WB_WBSel,
  input  EX_MEM_ebreak,
  input  MEM_WB_ecall,
  input  [4:0] EX_MEM_rdi,
  input  MEM_WB_ebreak,
  input  [31:0] EX_MEM_PC,
  input  [4:0] MEM_WB_rdi,
  input  [31:0] EX_MEM_PC_4,
  input  [31:0] MEM_WB_PC,
  input  [31:0] MEM_WB_PC_4,
  input  in_19
);

  PipelineReg32Bit pipelinereg32bit_1 (.DataIn(MemData), .WE(1'b1), .FLUSH(1'b0), .clk(in_19), .DataOut(MEM_WB_MemOut));
  PipelineReg32Bit pipelinereg32bit_2 (
    .DataIn(EX_MEM_ALUOut), .WE(1'b1), .FLUSH(1'b0), .clk(in_19), .DataOut(MEM_WB_ALUOut));
  PipelineReg1Bit pipelinereg1bit_1 (
    .DataIn(EX_MEM_RegWEn), .WE(1'b1), .FLUSH(1'b0), .clk(in_19), .DataOut(MEM_WB_RegWEn));
  PipelineReg2Bit pipelinereg2bit_1 (
    .DataIn(EX_MEM_WBSel), .WE(1'b1), .FLUSH(1'b0), .clk(in_19), .DataOut(MEM_WB_WBSel));
  PipelineReg1Bit pipelinereg1bit_2 (
    .DataIn(EX_MEM_ecall), .WE(1'b1), .FLUSH(1'b0), .clk(in_19), .DataOut(MEM_WB_ecall));
  PipelineReg1Bit pipelinereg1bit_3 (
    .DataIn(EX_MEM_ebreak), .WE(1'b1), .FLUSH(1'b0), .clk(in_19), .DataOut(MEM_WB_ebreak));
  PipelineReg5Bit pipelinereg5bit_1 (.DataIn(EX_MEM_rdi), .WE(1'b1), .FLUSH(1'b0), .clk(in_19), .DataOut(MEM_WB_rdi));
  PipelineReg32Bit pipelinereg32bit_3 (.DataIn(EX_MEM_PC), .WE(1'b1), .clk(in_19), .DataOut(MEM_WB_PC));  // open: FLUSH
  PipelineReg32Bit pipelinereg32bit_4 (
    .DataIn(EX_MEM_PC_4), .WE(1'b1), .clk(in_19), .DataOut(MEM_WB_PC_4));  // open: FLUSH

  // Other names for the same wires on the sheet: SysClk = in_19

  // Notes on the sheet:
  //   MEM_WB
endmodule
